# Fritzing sketch MoonlightFocuser (saved by Fritzing 0.9.3b)

parts:
  Board = Arduino Uno (Rev3)
  TEMPSENSOR = DS18B20 1-Wire Temperature Sensor [part_number=DS18B20]
  R1 = Resistor [tolerance=±5% resistance=4.7k package="0603 [SMD]"]
  C1 = Electrolytic Capacitor [capacitance=0.47mF voltage=16V package="100 mil [THT, electrolytic]"]
  Display = OLED 128x64 I2C Monochrome Display
  SWITCH_SPEED_(D12) = SWITCH-MOMENTARY-2 [package=tactile-pth]
  BACKWARD_(D11) = SWITCH-MOMENTARY-2 [package=tactile-pth]
  FORWARD_(D10) = SWITCH-MOMENTARY-2 [package=tactile-pth]
  R2 = Resistor [tolerance=±5% resistance=10k package="2512 [SMD]"]
  R3 = Resistor [tolerance=±5% resistance=10k package="1206 [SMD]"]
  R4 = Resistor [tolerance=±5% resistance=10k package="1206 [SMD]"]
  SM2 = 28BYJ-48 Stepper Motor [part_number=28BYJ-48]
  DRIVER = 28BYJ-48 Driver Module [part_number=ULN2003 package=THT]

nets:
  N1: Board.D10_PWM/SS, FORWARD_(D10).2, R4.Pin_0
  N2: Board.D11_PWM/MOSI, BACKWARD_(D11).2, R3.Pin_0
  N3: Board.D12/MISO, SWITCH_SPEED_(D12).2, R2.Pin_0
  GND: Board.GND, TEMPSENSOR.GND, C1.-, Display.GND, R2.Pin_1, R3.Pin_1, R4.Pin_1, DRIVER.GND
  N4: Board.A4/SDA, Display.SDA
  N5: Board.A5/SCL, Display.SCK
  N6: Board.D2, TEMPSENSOR.DQ, R1.Pin_0
  N7: Board.D4, DRIVER.IN4
  N8: Board.D5_PWM, DRIVER.IN3
  N9: Board.D6_PWM, DRIVER.IN2
  N10: Board.D7, DRIVER.IN1
  N11: Board.RESET, C1.+
  VDD: Board.5V, TEMPSENSOR.VDD, Display.VDD, BACKWARD_(D11).1, FORWARD_(D10).1, DRIVER.Vmotor
  N12: R1.Pin_1, SWITCH_SPEED_(D12).1
  N13: SM2.blue-pin, DRIVER.blue-pin
  N14: SM2.pink-pin, DRIVER.pink-pin
  N15: SM2.yellow-pin, DRIVER.yellow-pin
  N16: SM2.orange-pin, DRIVER.orange-pin
  N17: SM2.red-pin, DRIVER.red-pin

custom parts:
  28BYJ-48 Stepper Motor: Unipolar Stepper Motor 28BYJ-48 Top coil - pink & orange Bottom coil - blue & yellow Common rail - red Connector pins: blue - pink - yellow - orange - red
  28BYJ-48 Driver Module: Generic male header
